# Fritzing sketch 02-VirusBots (saved by Fritzing 0.9.3b)
breadboards: 1
stripboards: 1

parts:
  Εξάρτημα1 = Arduino Mega 2560 (Rev3)
  DHT11 = KY-015 Temperature & Humidity Sensor Module [package="Breakout board"]
  Καλωδιοταινία = KENT_LCD_CONN [package=ffc_16]
  U2 = KENT_LCD_CONN [package=ffc_16]
  PMS5003_Breakout = mystery part, 6 pins [chip_label="PM BREAKOUT"]

nets:
  N1: Εξάρτημα1.D19/RX1, PMS5003_Breakout.pin4
  N2: Εξάρτημα1.D18/TX1, PMS5003_Breakout.pin3
  N3: Εξάρτημα1.GND, DHT11.-, PMS5003_Breakout.pin2
  N4: Εξάρτημα1.D13_PWM, DHT11.S
  5V: Εξάρτημα1.5V, DHT11.Vin, PMS5003_Breakout.pin1
  N5: Καλωδιοταινία._RESET, U2.VSS2, U2.VCC
  N6: Καλωδιοταινία.BUSY, U2.CS, U2.VPWR1
  N7: Καλωδιοταινία.VSS1, U2.SI, U2.VPWR2
  N8: Καλωδιοταινία.SCK, U2.SO, U2.VSS3
  N9: Καλωδιοταινία.SO, U2.SCK, U2.VPWR3
  N10: Καλωδιοταινία.SI, U2.VSS1, U2.VSS4
  N11: Καλωδιοταινία.CS, U2.BUSY, U2.NC1
  N12: Καλωδιοταινία.VSS2, U2._RESET, U2.NC2

notes:
  PM Breakout Pins:
  1-> 5V
  2-> GND
  3-> TX
  4-> RX
  5-> RESET
  6-> EN

custom parts:
  KY-015 Temperature & Humidity Sensor Module: KY-015 temperature and humidity sensor module, provides a low-latency serial interface to measure humidity and temperature.
