# Fritzing sketch 04-VirusBots (saved by Fritzing 0.9.3b)
breadboards: 1
stripboards: 1

parts:
  Εξάρτημα1 = Arduino Mega 2560 (Rev3)
  LCD_20X4-I2C = LCD2004-I2C
  DHT11 = KY-015 Temperature & Humidity Sensor Module [package="Breakout board"]
  hc-sr1 = hc-sr04
  hc-sr2 = hc-sr04
  Καλωδιοταινία = KENT_LCD_CONN [package=ffc_16]
  U2 = KENT_LCD_CONN [package=ffc_16]
  PMS5003_Breakout = mystery part, 6 pins [chip_label="PM BREAKOUT"]
  Magnetic_Reed_Switch = Magnetic Door Switch [package=reed_switch_plastic]

nets:
  N1: Εξάρτημα1.D21/SCL, LCD_20X4-I2C.SCL
  N2: Εξάρτημα1.D20/SDA, LCD_20X4-I2C.SDA
  N3: Εξάρτημα1.D19/RX1, PMS5003_Breakout.pin4
  N4: Εξάρτημα1.D18/TX1, PMS5003_Breakout.pin3
  GND: Εξάρτημα1.GND, LCD_20X4-I2C.GND, DHT11.-, hc-sr1.GND, hc-sr2.GND, PMS5003_Breakout.pin2, Magnetic_Reed_Switch.2
  N5: Εξάρτημα1.D13_PWM, DHT11.S
  N6: Εξάρτημα1.D11_PWM, hc-sr2.Trig
  N7: Εξάρτημα1.D10_PWM, hc-sr2.Echo
  N8: Εξάρτημα1.D9_PWM, hc-sr1.Trig
  N9: Εξάρτημα1.D8_PWM, hc-sr1.Echo
  VCC: Εξάρτημα1.5V, LCD_20X4-I2C.VCC, DHT11.Vin, hc-sr1.VCC, hc-sr2.VCC, PMS5003_Breakout.pin1
  N10: Εξάρτημα1.D7_PWM, Magnetic_Reed_Switch.1
  N11: Καλωδιοταινία._RESET, U2.VSS2, U2.VCC
  N12: Καλωδιοταινία.BUSY, U2.CS, U2.VPWR1
  N13: Καλωδιοταινία.VSS1, U2.SI, U2.VPWR2
  N14: Καλωδιοταινία.SCK, U2.SO, U2.VSS3
  N15: Καλωδιοταινία.SO, U2.SCK, U2.VPWR3
  N16: Καλωδιοταινία.SI, U2.VSS1, U2.VSS4
  N17: Καλωδιοταινία.CS, U2.BUSY, U2.NC1
  N18: Καλωδιοταινία.VSS2, U2._RESET, U2.NC2

notes:
  PM Breakout Pins:
  1-> 5V
  2-> GND
  3-> TX
  4-> RX
  5-> RESET
  6-> EN

custom parts:
  LCD2004-I2C: A standard character display with 4x20 characters. Comes in many colors with LCM2004 IIC attached.
  KY-015 Temperature & Humidity Sensor Module: KY-015 temperature and humidity sensor module, provides a low-latency serial interface to measure humidity and temperature.
